// Digital circuit part_a.dig as structural Verilog
module part_a (
  input  in_0,
  input  in_1,
  input  in_2,
  output out_0
);

  wire and_1_out, and_2_out, and_3_out, and_4_out, and_5_out, and_6_out, and_7_out, nand_1_out, or_1_out,
       xor_1_out;

  nand nand_1 (nand_1_out, in_0, in_1);
  and and_1 (and_1_out, in_0, in_2);
  xor xor_1 (xor_1_out, in_1, in_2);
  and and_2 (and_2_out, in_0, in_1);
  and and_3 (and_3_out, in_1, in_2);
  and and_4 (and_4_out, in_0, in_2);
  or or_1 (or_1_out, and_1_out, xor_1_out);
  and and_5 (and_5_out, and_2_out, and_3_out);
  and and_6 (and_6_out, nand_1_out, or_1_out);
  and and_7 (and_7_out, and_5_out, and_4_out);
  or or_2 (out_0, and_6_out, and_7_out);
endmodule

/* Test case part_a_test:
in_0 in_1 in_2 out_0 

 0 0 0 0
 0 0 1 1
 0 1 0 1
 0 1 1 0
 1 0 0 0
 1 0 1 1
 1 1 0 0
 1 1 1 1
*/
