// Digital circuit part_c.dig as structural Verilog
module part_c (
  input  in_0,
  input  in_1,
  input  in_2,
  output out_0
);

  wire nfet_1_s, nfet_3_s, nfet_4_s, nfet_6_d, nfet_6_s, pfet_1_d, pfet_3_d, pfet_4_d, pfet_8_d, pfet_9_d;

  PFET pfet_1 (.G(in_0), .S(1'b0), .D(pfet_1_d));
  NFET nfet_1 (.G(in_0), .D(1'b0), .S(nfet_1_s));
  PFET pfet_2 (.G(in_2), .S(1'b0), .D(pfet_1_d));
  PFET pfet_3 (.G(in_0), .S(nfet_1_s), .D(pfet_3_d));
  PFET pfet_4 (.G(in_2), .S(pfet_3_d), .D(pfet_4_d));
  PFET pfet_5 (.G(in_2), .S(pfet_4_d), .D(1'b1));
  NFET nfet_2 (.G(in_2), .D(1'b0), .S(nfet_1_s));
  NFET nfet_3 (.G(in_0), .D(pfet_1_d), .S(nfet_3_s));
  NFET nfet_4 (.G(in_2), .D(nfet_3_s), .S(nfet_4_s));
  NFET nfet_5 (.G(in_2), .D(nfet_4_s), .S(1'b1));
  NFET nfet_6 (.G(in_0), .D(nfet_6_d), .S(nfet_6_s));
  PFET pfet_6 (.G(in_1), .S(nfet_6_s), .D(1'b1));
  PFET pfet_7 (.G(in_0), .S(1'b0), .D(nfet_6_d));
  NFET nfet_7 (.G(in_1), .D(1'b0), .S(nfet_6_d));
  PFET pfet_8 (.G(pfet_1_d), .S(1'b0), .D(pfet_8_d));
  PFET pfet_9 (.G(nfet_1_s), .S(pfet_8_d), .D(pfet_9_d));
  PFET pfet_10 (.G(nfet_6_d), .S(pfet_9_d), .D(out_0));
  NFET nfet_8 (.G(nfet_1_s), .D(out_0), .S(1'b1));
  NFET nfet_9 (.G(nfet_6_d), .D(out_0), .S(1'b1));
  NFET nfet_10 (.G(pfet_1_d), .D(out_0), .S(1'b1));
endmodule

/* Test case part_c_test:
in_0 in_1 in_2 out_0 

 0 0 0 1
 0 0 1 0
 0 1 0 1
 0 1 1 0
 1 0 0 1
 1 0 1 1
 1 1 0 0
 1 1 1 1
*/
